# Fritzing sketch board (saved by Fritzing 0.9.3b)
breadboards: 3

parts:
  Part1 = Arduino Uno (Rev3)
  Part3 = RFID-RC522-v2  # not connected
  R1 = Resistor [tolerance=±5% resistance=220 package=THT]
  R2 = Trimmer Potentiometer [maximum_resistance=10kΩ package=THT]
  LED1 = LED - 5mm [color="Blue (470nm)" package="5 mm [THT]"]
  U1 = 74HC595 [package="DIP16 [THT]"]
  LCD1 = LCD screen
  R3 = Resistor [tolerance=±5% resistance=220 package=THT]
  R4 = Resistor [tolerance=±5% resistance=220 package=THT]
  R5 = Resistor [tolerance=±5% resistance=220 package=THT]
  R6 = Resistor [tolerance=±5% resistance=220 package=THT]
  R7 = Resistor [tolerance=±5% resistance=220 package=THT]
  R8 = Resistor [tolerance=±5% resistance=220 package=THT]
  R9 = Resistor [tolerance=±5% resistance=220 package=THT]
  LED2 = LED - 5mm [color="Blue (470nm)" package="5 mm [THT]"]
  LED3 = LED - 5mm [color="Green (555nm)" package="5 mm [THT]"]
  LED4 = LED - 5mm [color="Green (555nm)" package="5 mm [THT]"]
  LED5 = LED - 5mm [color="Red (633nm)" package="5 mm [THT]"]
  LED6 = LED - 5mm [color="Red (633nm)" package="5 mm [THT]"]
  LED7 = LED - 5mm [color="Yellow (585nm)" package="5 mm [THT]"]
  LED8 = LED - 5mm [color="Yellow (585nm)" package="5 mm [THT]"]
  J1 = Basic Servo

nets:
  N1: Part1.A0, U1.SH_CP
  N2: Part1.A1, U1.ST_CP
  N3: Part1.A2, U1.DS
  N4: Part1.D8, LCD1.DB7
  N5: Part1.D2, J1.pulse
  N6: Part1.D3_PWM, LCD1.RS
  N7: Part1.D4, LCD1.E
  N8: Part1.D5_PWM, LCD1.DB4
  N9: Part1.D6_PWM, LCD1.DB5
  N10: Part1.D7, LCD1.DB6
  VCC: Part1.5V, R2.leg1, U1.MR, U1.VCC, LCD1.VDD, LCD1.LED+, J1.vcc
  GND: Part1.GND, R2.leg2, LED1.cathode, U1.OE, LCD1.VSS, LCD1.R/W, LCD1.LED-, LED2.cathode, LED3.cathode, LED4.cathode, LED5.cathode, LED6.cathode, LED7.cathode, LED8.cathode, J1.gnd
  N11: R1.Pin_0, U1.Q0
  N12: R1.Pin_1, LED3.anode
  N13: R2.wiper, LCD1.V0
  N14: LED1.anode, R5.Pin_1
  N15: U1.Q1, R4.Pin_0
  N16: U1.Q2, R5.Pin_0
  N17: U1.Q4, R6.Pin_0
  N18: U1.Q5, R7.Pin_0
  N19: U1.Q6, R8.Pin_0
  N20: U1.Q7, R9.Pin_0
  N21: U1.GND, R3.Pin_0
  N22: R3.Pin_1, LED8.anode
  N23: R4.Pin_1, LED4.anode
  N24: R6.Pin_1, LED2.anode
  N25: R7.Pin_1, LED5.anode
  N26: R8.Pin_1, LED6.anode
  N27: R9.Pin_1, LED7.anode

custom parts:
  RFID-RC522-v2: A simple China made RFID-RC522 Reader; do check the pin labels, as this is a MFRC522 based clone.
